# Fritzing sketch fader-test-diagram (saved by Fritzing 0.9.3b)
breadboards: 1

parts:
  Part1 = Arduino Nano (Rev3.0)
  R1 = Resistor [tolerance=±5% resistance=10k package=THT]
  ANT1 = Antenna
  R2 = Slide Potentiometer [maximum_resistance=100kΩ]

nets:
  N1: Part1.GND, R2.leg2
  N2: Part1.5V, R2.leg1
  N3: Part1.A1, R2.wiper
  N4: Part1.A0, R1.Pin_1
  N5: R1.Pin_0, ANT1.antenna_lead
